# Fritzing sketch estagio (saved by Fritzing 0.9.3b)
circuit board: 8.46667cm x 5.64444cm
breadboards: 1

parts:
  Componente1 = Bluetooth HC-05 Macho
  U1 = LCD-16X2 [package=lcd-16x2_noholes]
  Componente2 = Adafruit I2C+SPI LCD Backpack [part_number="Adafruit #292"]
  U2 = 4-Channel 5v Relay Shield [package=relay-4ch5v10a]
  Componente3 = Arduino Uno (Rev3)
  LED1 = LEDs [package=led10mm]
  LED2 = LEDs [package=led10mm]
  LED3 = LEDs [package=led10mm]
  LED4 = LEDs [package=led10mm]

nets:
  N1: Componente1.TXD, Componente3.D0/RX
  N2: Componente1.RXD, Componente3.D1/TX
  VCC: Componente1.VCC, U2.VCC, U2.K1-Off, U2.K2-Off, U2.K3-Off, U2.K4-Off, Componente3.5V
  GND: Componente1.GND, U2.GND, Componente3.GND, LED1.C, LED2.C, LED3.C, LED4.C
  VSS: U1.VSS, U1.R_W, Componente2.GND
  VDD: U1.VDD, U1.A, Componente2.VCC
  N3: U1.VO, Componente2.CONTRAST
  N4: U1.RS, Componente2.RS
  N5: U1.E, Componente2.E
  N6: U1.DB0, Componente2.DB0
  N7: U1.DB1, Componente2.DB1
  N8: U1.DB2, Componente2.DB2
  N9: U1.DB3, Componente2.DB3
  N10: U1.DB4, Componente2.DB4
  N11: U1.DB5, Componente2.DB5
  N12: U1.DB6, Componente2.DB6
  N13: U1.DB7, Componente2.DB7
  N14: U1.K, Componente2.LEDK
  N15: U2.IN1, Componente3.D5_PWM
  N16: U2.IN2, Componente3.D4
  N17: U2.K1-On, LED1.A
  N18: U2.K2-On, LED2.A
  N19: U2.IN4, Componente3.D2
  N20: U2.K3-On, LED3.A
  N21: U2.K4-On, LED4.A
  N22: U2.IN3, Componente3.D3_PWM

custom parts:
  Adafruit I2C+SPI LCD Backpack: LCD backpacks reduce the number of pins needed to connect to an LCD. LCDs are a fun and easy way to have your microcontroller project talk back to you. Character LCDs are common, and easy to get, available in tons of colors and sizes. We've written tutorials on using character LCDs with an Arduino (or similar microcontroller) but find that the number of pins necessary to control the LCD can be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
  4-Channel 5v Relay Shield: 4 Channel 5v Relay Shield w. 2x SPD-06VDC-SD-C
  LEDs: LEDs Standard schematic elements and footprints for 5mm, 3mm, 1206, and 0603 sized LEDs. 5mm - Spark Fun Electronics SKU : COM-00529 (and others)

// code stored in the sketch: programa_do_estagio1.ino
#include <SoftwareSerial.h>

SoftwareSerial mySerial(0,1);//0-rx, 1-tx

int rele = 5; //define porta 5 como rele
int rele1 = 4; //define porta 4 como rele1
int rele2 = 3; //define porta 3 como rele2
int rele3 = 2; //define porta 2 como rele3 

void setup(){
  mySerial.begin(9600); //define a comunicção serial em 9600
  pinMode(rele, OUTPUT); //declara rele como pino de saida
  pinMode(rele1, OUTPUT); //declara rele1 como pino de saida
  pinMode(rele2, OUTPUT); //declara rele2 como pino de saida
  pinMode(rele3, OUTPUT); //declara rele3 como pino de saida
  }
void loop(){
  char caracter = mySerial.read(); //faz leitura do cactere

  if(caracter == 'A'){ //se identifica caracter 'A'
    digitalWrite(rele, HIGH); //liga rele
    }
  if(caracter == 'a'){ //se identifica caracter 'a'
    digitalWrite(rele, LOW); //desliga rele
    }
  if(caracter == 'B'){ //se identifica caracter 'B'
    digitalWrite(rele1, HIGH); //liga rele1
    }
  if(caracter == 'b'){ //se identifica caracter 'b'
    digitalWrite(rele1, LOW); //desliga rele1
    }
  if(caracter == 'C'){ //se identifica caracter 'C'
    digitalWrite(rele2, HIGH); //liga rele2
    }
  if(caracter == 'c'){ //se identifica caracter 'c'
    digitalWrite(rele2, LOW); //desliga rele2
    }
  if(caracter == 'D'){ //se identifica caracter 'D'
    digitalWrite(rele3, HIGH); //liga rele3
    }
  if(caracter == 'd'){ //se identifica caracter 'd'
    digitalWrite(rele3, LOW); //desliga rele3
    }
}
